# Fritzing sketch 3_IoT_Bank_Security_Telegram_bb (saved by Fritzing 0.9.10b)

parts:
  Part1 = Arduino Uno (Rev3) - ICSP
  M1 = DOIT Esp32 DevKit v1 (30 pins long, 11 pins width) [part_number=ESP32S-PIN30]
  Mod1 = KY-018 Photoresistor Module [package="Breakout board"]
  Part2 = LCD1602-I2C
  Mod2 = KY-015 Temperature & Humidity Sensor Module [package="Breakout board"]
  Mod3 = L298N DC motor driver
  J1 = Piezo Speaker
  Mod4 = KY-008 Laser Transmitter Module [package="Breakout board"]
  LED1 = smd LED [color="Red (633nm)" package="1206 [SMD]"]
  LED2 = smd LED [color="Red (633nm)" package="1206 [SMD]"]
  M2 = fc-51 [package=THT]
  M3 = fc-51 [package=THT]
  M4 = DC Motor [voltage_(max)=6V voltage_(min)=3V]
  BAT1 = BC9VPC [package=bc9vpc]

nets:
  N1: Part1.A4/SDA, Part2.SDA
  N2: Part1.A5/SCL, Part2.SCL
  N3: Part1.D9_PWM, Mod3.IN1
  N4: Part1.D10_PWM/SS, Mod3.ENA
  N5: Part1.D2, M2.pin1
  N6: Part1.D3_PWM, M3.pin1
  N7: Part1.D4, J1.pin2
  N8: Part1.D5_PWM, Mod2.S
  N9: Part1.D6_PWM, M1.D4
  N10: Part1.D7, M1.D5
  N11: Part1.IOREF, M2.pin3
  5V: Part1.5V, Part2.VCC
  GND: Part1.GND, Part2.GND, M2.pin2
  N12: M1.GND, Mod1.-
  N13: M1.D18, Mod1.S
  N14: M1.D14, Mod4.S
  N15: M1.D12, LED2.anode
  N16: M1.D13, LED1.anode
  VIN: M1.VIN, Mod1.Vin
  N17: Mod2.-, J1.pin1
  N18: Mod3.OUT1, M4.pin_2
  N19: Mod3.OUT2, M4.pin_1
  N20: Mod3.12V, Mod3.5V-ENA-JMP-O, BAT1.V+
  N21: Mod4.-, LED2.cathode

custom parts:
  DOIT Esp32 DevKit v1 (30 pins long, 11 pins width): The DOIT Esp32 DevKit v1 is one of the development board created by DOIT to evaluate the ESP-WROOM-32 module. It is based on the ESP32 microcontroller that boasts Wifi, Bluetooth, Ethernet and Low Power support all in a single chip. (vanepp) made breadboard work, adjusted pin numbering and labels and reduced size of schematic and cleaned up pcb. This chip is 30pins long (2 x15) and 11 pins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
  KY-018 Photoresistor Module: KY-018 Photoresistor module, used to measure light intensity. It can determine the presence or absence of light.
  LCD1602-I2C: A standard character display, usually with 2x16 characters. Comes in many colors with LCM1602 IIC attached.
  KY-015 Temperature & Humidity Sensor Module: KY-015 temperature and humidity sensor module, provides a low-latency serial interface to measure humidity and temperature.
  L298N DC motor driver: 2x DC motor driver with 78M05 positive voltage regulator (7..35 V) L298N: max 46 V, 2 A Set 5 V Enable jumper to enable 5 V regultor (needed for the L298N) and +5 V output at screw terminal or supply external +5 V at screw terminal Set ENA and/or ENB to +5 V to enable motor permanently or supply ENA and/or ENB with PWM signal IN1 and IN2 set rotation directory for motor A (OUT1/OUT2) IN2 and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
  KY-008 Laser Transmitter Module: KY-008 Laser Transmitter Module, emits a dot shaped red laser beam.
